# Fritzing sketch Simon Says Schaltplan (saved by Fritzing 0.9.3b)
breadboards: 1

parts:
  U1 = NodeMCU V3.0
  R1 = Resistor [tolerance=±5% resistance=1k package="0805 [SMD]"]
  R2 = Resistor [tolerance=±5% resistance=1k package="0805 [SMD]"]
  R3 = Resistor [tolerance=±5% resistance=100 package="0805 [SMD]"]
  R4 = Resistor [tolerance=±5% resistance=1k package="0805 [SMD]"]
  R5 = Resistor [tolerance=±5% resistance=10k package="0805 [SMD]"]
  R6 = Resistor [tolerance=±5% resistance=330 package="0805 [SMD]"]
  LED1 = LED - 5mm [color="Red (633nm)" package="5 mm [THT]"]
  S1 = Pushbutton [package=THT]
  S2 = Pushbutton [package=THT]
  LED2 = LED - 5mm [color="Yellow (595nm)" package="5 mm [THT]"]
  S3 = Pushbutton [package=THT]
  LED3 = LED - 5mm [color="Green (565nm)" package="5 mm [THT]"]
  S4 = Pushbutton [package=THT]
  LED4 = LED - 5mm [color="Blue (505nm)" package="5 mm [THT]"]

nets:
  N1: U1.D1, LED2.anode
  N2: U1.D2, LED1.anode
  N3: U1.3V3, S1.leg0, S2.leg0, S3.leg0, S4.leg0
  N4: U1.GND#6, U1.GND#13, U1.GND#16, U1.GND#33, R2.Pin_0, LED1.cathode, LED2.cathode, LED3.cathode, LED4.cathode
  N5: U1.D6, LED3.anode
  N6: U1.D7, LED4.anode
  N7: U1.A0, R1.Pin_1
  N8: R1.Pin_0, R2.Pin_1, R3.Pin_1, R4.Pin_1, R5.Pin_1, R6.Pin_1
  N9: R3.Pin_0, S4.leg1
  N10: R4.Pin_0, S3.leg1
  N11: R5.Pin_0, S2.leg1
  N12: R6.Pin_0, S1.leg1

custom parts:
  NodeMCU V3.0: ESP8266 based NodeMCU
